# Fritzing sketch wiring_schem (saved by Fritzing 0.9.10b)
circuit board: 8.16998cm x 5.5512cm
breadboards: 1

parts:
  part = Raspberry Pi Pico
  part_2 = E3F-DS30C4 [part_number="Proximity Sensor" package=THT]
  part_3 = 74HC595 SMD [package="SO16 [SMD]"]
  part_4 = HS420561K [part_number="Four-digit Seven-Segment Display" package="DIP (Dual Inline) [THT]"]
  part_5 = Buzzer 12mm [part_number=Buzzer package=buzzer-12mm-ns]
  part_6 = 74HC595 SMD [package="SO16 [SMD]"]

nets:
  GND: part.pin_13, part.pin_33, part.pin_38, part_2.pin3, part_3.GND, part_3.OE, part_5.1, part_6.GND, part_6.OE
  N1: part.pin_21, part_2.pin2
  N2: part.pin_22, part_5.2
  N3: part.pin_24, part_6.DS
  N4: part.pin_25, part_3.ST_CP, part_6.ST_CP
  N5: part.pin_26, part_3.SH_CP, part_6.SH_CP
  VCC: part.pin_39, part_2.pin1, part_3.VCC, part_6.VCC
  N6: part_3.Q1, part_4.pin7
  N7: part_3.Q2, part_4.pin4
  N8: part_3.Q3, part_4.pin2
  N9: part_3.Q4, part_4.pin1
  N10: part_3.Q5, part_4.pin_10
  N11: part_3.Q6, part_4.pin5
  N12: part_3.Q7, part_4.pin3
  N13: part_3.DS, part_6.Q7'
  N14: part_3.Q0, part_4.pin_11
  N15: part_4.pin6, part_6.Q3
  N16: part_4.pin8, part_6.Q2
  N17: part_4.pin_9, part_6.Q1
  N18: part_4.pin_12, part_6.Q0

custom parts:
  Raspberry Pi Pico: Raspberry Pi Pico. Based around the RP2040 microcontroller the Pico is a low cost microcontroller device bringing Raspberry Pi quality, cost, and easy of use to the microcontroller space. Jan 2021, Split part in to two versions: tht (this one) and SMD. This one will drill holes for a .1 in header in pcb to allow plugging in the module as well as providing pads to solder the module to the top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
  E3F-DS30C4: Omron E3F-DS30C4 Infrared Proximity Sensor module. 0 30CM (adjustable) range 6-36V NPN NO output
